# Fritzing sketch DHT11_OLED (saved by Fritzing 0.9.3b)
breadboards: 1

parts:
  元件1 = Arduino Nano (Rev3.0)
  元件2 = SPI OLED Monochrome 128x64 0.96 inch
  DHT1 = DHT11 Humitidy and Temperature Sensor
  R1 = Resistor [tolerance=±5% resistance=220 package=THT]

nets:
  GND: 元件1.GND, 元件2.GND
  N1: 元件1.D2, 元件2.SCK
  N2: 元件1.D3, 元件2.SDA
  N3: 元件1.D4, 元件2.RES
  N4: 元件1.D5, 元件2.DC
  N5: 元件1.D6, 元件2.CS
  N6: 元件1.D7, DHT1.DATA, R1.Pin_1
  5V: 元件1.5V, 元件2.VDD
  N7: DHT1.VDD, R1.Pin_0

custom parts:
  SPI OLED Monochrome 128x64 0.96 inch: Unknown 128x64 0.96 inch 128x64 SPI Monochrome OLED display
  DHT11 Humitidy and Temperature Sensor: DHT11 Humidity and Temperature Sensor
